# Fritzing sketch Nano_Sound_Sensor_Oled (saved by Fritzing 0.9.9b)
breadboards: 1

parts:
  OLED_I2C1 = OLED 128x64 I2C Monochrome Display
  Part1 = KY-037 High Sensitivity Sound Detection Module [package="Breakout board"]
  Part2 = Arduino Nano (Rev3.0)

nets:
  N1: OLED_I2C1.SDA, Part2.A4
  N2: OLED_I2C1.SCK, Part2.A5
  N3: Part1.A0, Part2.A0
  N4: Part1.G, Part2.GND
  N5: Part1.+, Part2.5V

custom parts:
  KY-037 High Sensitivity Sound Detection Module: KY-037 high sensitivity sound detection module is an analog/digital sensor that uses a condenser microphone to observe changes in environment noise.
